# Fritzing sketch fritzing (saved by Fritzing 0.9.8b)
breadboards: 1

parts:
  J1 = STM32 Nucleo boards
  R1 = Resistor [tolerance=±5% resistance=220 package="2010 [SMD]"]
  R2 = Temperature Sensor (Thermistor) [thermistor_type=NTC package=THT]

nets:
  N1: J1.A0, R2.pin_1
  N2: J1.GND, R1.Pin_0
  N3: J1.VIN, R1.Pin_1, R2.pin_0
